# Fritzing sketch FanControllerBoard (saved by Fritzing 0.9.10b)
circuit board: 7.88529cm x 4.12044cm
breadboards: 1

parts:
  Tach_From_Fans = female pin header, 4 pins [form="♀ (female)"]
  A0-3 = female pin header, 4 pins [form="♀ (female)"]
  PWM_from_Fans = female pin header, 4 pins [form="♀ (female)"]
  2_Amp_GND = female pin header, 4 pins [form="♀ (female)"]
  0_5_Amp_+12V_to_Fans = female pin header, 4 pins [form="♀ (female)"]
  2_Amp_+12V = female pin header, 4 pins [form="♀ (female)"]
  High_PWM_+3_3V_(EN)_and_GND = Screw terminal - 2 pins [package=THT]
  R1 = Resistor [tolerance=±5% power=0.25 resistance=540 package=THT]
  R2 = Resistor [tolerance=±5% power=0.25 resistance=540 package=THT]
  R3 = Resistor [tolerance=±5% power=0.25 resistance=540 package=THT]
  R4 = Resistor [tolerance=±5% power=0.25 resistance=540 package=THT]
  0_5_Amp_Fan_GNDs = female pin header, 4 pins [form="♀ (female)"]
  VIN+_VIN- = Screw terminal - 2 pins [package=THT]
  G_G_+3_3_+3_3 = female pin header, 4 pins [form="♀ (female)"]
  GPIO_PWM_+_Enable = female pin header, 5 pins [form="♀ (female)"]

nets:
  N1: Tach_From_Fans.pin1, A0-3.pin1, R1.Pin_1
  N2: Tach_From_Fans.pin2, A0-3.pin2, R2.Pin_1
  N3: Tach_From_Fans.pin3, A0-3.pin3, R3.Pin_1
  N4: Tach_From_Fans.pin4, A0-3.pin4, R4.Pin_1
  N5: PWM_from_Fans.pin1, GPIO_PWM_+_Enable.pin1
  N6: PWM_from_Fans.pin2, GPIO_PWM_+_Enable.pin2
  N7: PWM_from_Fans.pin3, GPIO_PWM_+_Enable.pin3
  N8: PWM_from_Fans.pin4, GPIO_PWM_+_Enable.pin4
  N9: 2_Amp_GND.pin1, 2_Amp_GND.pin2, 2_Amp_GND.pin3, 2_Amp_GND.pin4, 0_5_Amp_Fan_GNDs.pin1, 0_5_Amp_Fan_GNDs.pin2, 0_5_Amp_Fan_GNDs.pin3, 0_5_Amp_Fan_GNDs.pin4, VIN+_VIN-.pin2
  N10: 0_5_Amp_+12V_to_Fans.pin1, 0_5_Amp_+12V_to_Fans.pin2, 0_5_Amp_+12V_to_Fans.pin3, 0_5_Amp_+12V_to_Fans.pin4, 2_Amp_+12V.pin1, 2_Amp_+12V.pin2, 2_Amp_+12V.pin3, 2_Amp_+12V.pin4, VIN+_VIN-.pin1
  N11: High_PWM_+3_3V_(EN)_and_GND.pin1, G_G_+3_3_+3_3.pin1, G_G_+3_3_+3_3.pin2
  N12: High_PWM_+3_3V_(EN)_and_GND.pin2, GPIO_PWM_+_Enable.pin5
  N13: R1.Pin_0, R2.Pin_0, R3.Pin_0, R4.Pin_0, G_G_+3_3_+3_3.pin3, G_G_+3_3_+3_3.pin4

notes:
  +3.3V Pullup resistors
  +3.3V
  GND
  2AMP 12V ciruit
