# Fritzing sketch FanControllerFinal (saved by Fritzing 0.9.10b)
circuit board: 8.43606cm x 6.65667cm
breadboards: 1

parts:
  A0-3 = female pin header, 4 pins [form="♀ (female)"]
  To_High_PWM_+3_3V_(EN)_and_GND = Screw terminal - 2 pins [package=THT]
  R1 = Resistor [tolerance=±5% power=0.25 resistance=540 package=THT]
  R2 = Resistor [tolerance=±5% power=0.25 resistance=540 package=THT]
  R3 = Resistor [tolerance=±5% power=0.25 resistance=540 package=THT]
  R4 = Resistor [tolerance=±5% power=0.25 resistance=540 package=THT]
  From_XY-GMOS_OUT-_OUT+ = Screw terminal - 2 pins [package=THT]
  G_+3_3_LPBK0_LPBK1 = female pin header, 4 pins [form="♀ (female)"]
  PWM_+_Enable = female pin header, 5 pins [form="♀ (female)"]
  Unused_pins = female pin header, 7 pins [form="♀ (female)"]
  C2 = Ceramic Capacitor [capacitance=100nF voltage=35V package="200 mil [THT, multilayer]"]
  R5 = Resistor [tolerance=±5% resistance=1 power=0.25 package=THT]
  Part1 = DB25F

nets:
  N1: A0-3.pin1, R1.Pin_1, Part1.pin8
  N2: A0-3.pin2, R2.Pin_1, Part1.pin7
  N3: A0-3.pin3, R3.Pin_1, Part1.pin6
  N4: A0-3.pin4, R4.Pin_1, Part1.pin5
  N5: To_High_PWM_+3_3V_(EN)_and_GND.pin1, G_+3_3_LPBK0_LPBK1.pin1
  N6: To_High_PWM_+3_3V_(EN)_and_GND.pin2, PWM_+_Enable.pin5
  N7: R1.Pin_0, R2.Pin_0, R3.Pin_0, R4.Pin_0, G_+3_3_LPBK0_LPBK1.pin2
  N8: From_XY-GMOS_OUT-_OUT+.pin1, C2.1, Part1.pin14, Part1.pin15, Part1.pin16, Part1.pin17
  N9: From_XY-GMOS_OUT-_OUT+.pin2, C2.0, R5.Pin_1
  N10: G_+3_3_LPBK0_LPBK1.pin3, Part1.pin25
  N11: G_+3_3_LPBK0_LPBK1.pin4, Part1.pin13
  N12: PWM_+_Enable.pin1, Part1.pin1
  N13: PWM_+_Enable.pin2, Part1.pin2
  N14: PWM_+_Enable.pin3, Part1.pin3
  N15: PWM_+_Enable.pin4, Part1.pin4
  N16: Unused_pins.pin1, Part1.pin18
  N17: Unused_pins.pin2, Part1.pin19
  N18: Unused_pins.pin3, Part1.pin20
  N19: Unused_pins.pin4, Part1.pin21
  N20: Unused_pins.pin5, Part1.pin22
  N21: Unused_pins.pin6, Part1.pin23
  N22: Unused_pins.pin7, Part1.pin24
  N23: R5.Pin_0, Part1.pin9, Part1.pin10, Part1.pin11, Part1.pin12

notes:
  +3.3V Pullup resistors
  +3.3V
  GND
  2AMP 12V ciruit
  Public Invention, 2023, for NASA
  Fan Control 0.12CERN OH v2 Strong Reciprocal
