# Fritzing sketch RibbonFish (saved by Fritzing 0.9.10b)
breadboards: 3

parts:
  Part1 = Arduino Due (Rev2b)
  BB1 = 4-Line Bi-Directional Level Shifter
  Sensirion_Flow_Sensor = IC, SIP package, 4 pins [chip_label="Sensirion SFM300"]
  Part2 = Adafruit Thermocouple Amplifier with 1-Wire Breakout Board - MAX31850K [part_number="Adafruit #1727"]
  Part3 = Adafruit Thermocouple Amplifier with 1-Wire Breakout Board - MAX31850K [part_number="Adafruit #1727"]
  R1 = Resistor [tolerance=±5% resistance=4700 package="2010 [SMD]"]
  TF800A12K = female pin header, 3 pins [form="♀ (female)"]
  Sanyo_Dual_Fan_Connector = female pin header, 10 pins [form="♀ (female)"]
  Power_plug1 = Power plug
  F1 = Fan - 4 wire [package=THT]
  F2 = Fan - 4 wire [package=THT]
  F3 = Fan - 4 wire [package=THT]
  F4 = Fan - 4 wire [package=THT]
  R2 = Resistor [tolerance=±5% resistance=560 package="0805 [SMD]"]
  R3 = Resistor [tolerance=±5% resistance=560 package="0805 [SMD]"]
  R4 = Resistor [tolerance=±5% resistance=560 package="0805 [SMD]"]
  R10 = Resistor [tolerance=±5% resistance=560 package="0805 [SMD]"]
  XY-GMOS_MOTOR_DRIVER = IC, DIP package, 6 pins [chip_label=IC]
  R11 = Resistor [tolerance=±5% resistance=10000 package="0603 [SMD]"]
  R12 = Resistor [tolerance=±5% resistance=10000 package="0603 [SMD]"]
  GGLabsSSR1 = female pin header, 3 pins [form="♀ (female)"]

nets:
  N1: Part1.D18/TX1, TF800A12K.pin2
  N2: Part1.D19/RX1, TF800A12K.pin3
  N3: Part1.D20/SDA3, BB1.A4
  N4: Part1.D21/SCL3, BB1.A3
  N5: Part1.IOREF, BB1.LV, R1.Pin_1, R2.Pin_0, R3.Pin_0, R4.Pin_0, R10.Pin_0
  N6: Part1.5V, BB1.HV, Sensirion_Flow_Sensor.pin1
  GND: Part1.GND, BB1.GND, Sensirion_Flow_Sensor.pin2, Part2.GND, Part3.GND, TF800A12K.pin1, XY-GMOS_MOTOR_DRIVER.pin4, R11.Pin_1, R12.Pin_1, GGLabsSSR1.pin1
  N7: Part1.D8_PWM, XY-GMOS_MOTOR_DRIVER.pin3
  N8: Part1.D9_PWM, Sanyo_Dual_Fan_Connector.pin1, F1.PWM
  N9: Part1.D10_PWM/SS0, Sanyo_Dual_Fan_Connector.pin3, F2.PWM
  N10: Part1.D11_PWM, Sanyo_Dual_Fan_Connector.pin6, F3.PWM
  N11: Part1.D12_PWM, Sanyo_Dual_Fan_Connector.pin8, F4.PWM
  N12: Part1.D4_PWM/SS1, Part2.DATA, Part3.DATA, R1.Pin_0
  N13: Part1.D50, R12.Pin_0, GGLabsSSR1.pin2
  N14: Part1.D51, R11.Pin_0, GGLabsSSR1.pin3
  N15: BB1.B3, Sensirion_Flow_Sensor.pin3
  N16: BB1.B4, Sensirion_Flow_Sensor.pin4
  GND_2: Sanyo_Dual_Fan_Connector.pin9, F1.GND, F2.GND, F3.GND, F4.GND, XY-GMOS_MOTOR_DRIVER.pin5
  N17: Sanyo_Dual_Fan_Connector.pin10, F1.Power, F2.Power, F3.Power, F4.Power, XY-GMOS_MOTOR_DRIVER.pin6
  N18: Power_plug1.GND, XY-GMOS_MOTOR_DRIVER.pin2
  N19: Power_plug1.VCC, XY-GMOS_MOTOR_DRIVER.pin1
  N20: F1.Tach, R3.Pin_1
  N21: F2.Tach, R2.Pin_1
  N22: F3.Tach, R4.Pin_1
  N23: F4.Tach, R10.Pin_1

notes:
  5V direct to flow sensor
  Note: This is obviously modular to add additional boards for a full 6-stack oxygen engine. This setup is using "parasitic power".
  TF800A12K uses Serial1, and we tie the ground of the power supply to the ground just to make sure we have a clean ground.
  This connector was made to organize and decrease the number of wires. Of the 10 pins, the las two (11 and 12) are GND and +12V.
  NOTE! Keep this 12V circuit separate! You can call a Due by sinking the fan power through its ground.
  This is best accomplished as a 12V power jack, just like the Due, but don't use that.
  https://www.delta-fan.com/Download/Spec/GFC0412DS-DV17.pdf - this is electrically four 4-wire fans. I've tied 1V power and GND together and brought the 4 tachs and 4 PWMS wires into the header.
  The Tack pulls down, so you need pull resistors to 3.3V for reading a signal. I've learned the hard way this resistory has to be relatively low resistance of the interrupt will trigger far too often. I use a 560 Ohm resistor and it works, but 3.47K Ohm does not!
  This image is wrong; this part is the XY-GMOS PWM DC speed controller board, which is really a 6- connector part: vin+, vin-, motor+, motor-, GND, HIGH/PWM. This is needed because the stupid fans won't turn off completely with any PWM signal I can generate with a DUE. This is used ONLY to cut power completely or provide full power. It is very important to keep the GND/PWM signals isolated from the 12V PWM signals.

custom parts:
  4-Line Bi-Directional Level Shifter: 4-Channel Bi-Directional Level Shifter
  Adafruit Thermocouple Amplifier with 1-Wire Breakout Board - MAX31850K: Thermocouples are very sensitive, requiring a good amplifier with a cold-compensation reference. So far we've carried the very nice MAX31855 which is an SPI interface thermocouple amplifier. The '855 is great but if you have a lot of thermocouples to measure it isn't terribly easy to use. That's why we are also carrying the new '850 model from Maxim - it's a "1-Wire" thermocouple amp which can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
  Fan - 4 wire: Fan, 4 wire with tach.
