# Fritzing sketch SanyoAceBreakout (saved by Fritzing 0.9.10b)
circuit board: 6.19996cm x 2.9642cm
perfboards: 1

parts:
  Part1 = Arduino Due (Rev2b)
  F1 = Fan - 4 wire [package=THT]
  J1 = Camdenboss CTB0158-2 [part_number=CTB0158-2 package=THT]
  J2 = Camdenboss CTB0158-2 [part_number=CTB0158-2 package=THT]
  J3 = Camdenboss CTB0158-2 [part_number=CTB0158-2 package=THT]
  R2 = Resistor [tolerance=±5% resistance=2.8k power=0.25 package=THT]
  R1 = Resistor [tolerance=±5% resistance=22k power=0.25 package=THT]

nets:
  N1: Part1.A0, F1.Tach, J1.pin1, J1.pin2, R1.Pin_0
  N2: Part1.IOREF, J3.pin1, R1.Pin_1
  N3: Part1.GND, J3.pin2, R2.Pin_0
  N4: Part1.D9_PWM, F1.PWM, J2.pin1, J2.pin2, R2.Pin_1

notes:
  This diagram describers our working circuit for the SanyAceB97 4-wire fan. There is some question that this approach is really in spec. We may design a system with level shifters later. Since this is goint to be done by hand, I'm designing it on a perfobard. The fan and the Due are just for show!

custom parts:
  Fan - 4 wire: Fan, 4 wire with tach.
